// Logisim project cpu-16bit-io.circ as structural Verilog: 9 circuits, main circuit main
module main (
  input  in_1,
  input  Reset,
  input  [6:0] in_3,
  input  [6:0] in_4,
  input  [6:0] in_5,
  input  [6:0] in_6,
  input  [6:0] in_7,
  input  [15:0] in_8,
  input  in_9
);

  wire and_1_out, and_2_out, and_3_out, bus_control_1_alu_enable, bus_control_1_bus_read,
       bus_control_1_bus_write, bus_control_1_reg_write, clock, comparator_1_eq, comparator_2_eq,
       comparator_3_eq, comparator_4_eq, consume, cycle, enable, keydata, not_1_out, not_2_out, not_3_out,
       not_4_out, t_ff_1_qn;
  wire [3:0] decoder_1_operand1, decoder_1_operand2, decoder_1_operand3, opcode;
  wire [6:0] bit_extender_1_out, keyboard_1_data;
  wire [7:0] bus_control_1_bus_addr, mmm, multiplexer_1_out, pc_control_1_pc_new, register_2_q;
  wire [15:0] alu_1_bus_out, bit_extender_2_out, data, n16_register_file_1_b, ram_1_data, register_1_q;

  Register #(.width(16)) register_1 (.D(alu_1_bus_out), .Q(register_1_q), .clk(and_1_out), .clr(Reset));  // open: en
  not not_1 (not_1_out, clock);
  Decoder decoder_1 (
    .instruction(register_1_q), .opcode(opcode), .operand1(decoder_1_operand1),
    .operand2(decoder_1_operand2), .operand3(decoder_1_operand3), .immediate(mmm));
  T_Flip_Flop t_ff_1 (.clk(not_1_out), .T(1'b1), .Q(cycle), .Qn(t_ff_1_qn));  // open: preset, reset, en
  Clock u_Clock (.out(clock));
  and and_1 (and_1_out, t_ff_1_qn, clock);
  and and_2 (and_2_out, cycle, clock);
  _16_register_file u_16_register_file_1 (
    .d(alu_1_bus_out), .Clk(bus_control_1_reg_write), .Rd(decoder_1_operand1), .Clr(Reset),
    .Ra(decoder_1_operand2), .Rb(decoder_1_operand3), .a(data), .b(n16_register_file_1_b));
  ALU alu_1 (
    .a(data), .b(n16_register_file_1_b), .op(opcode), .imm(mmm), .enable(bus_control_1_alu_enable),
    .bus_out(alu_1_bus_out));
  PC_control pc_control_1 (.PC_new(pc_control_1_pc_new), .op(opcode), .a(data), .imm(mmm), .PC_old(register_2_q));
  Register register_2 (.D(pc_control_1_pc_new), .Q(register_2_q), .clk(and_2_out), .clr(Reset));  // open: en
  bus_control bus_control_1 (
    .a(data), .reg_write(bus_control_1_reg_write), .ALU_enable(bus_control_1_alu_enable), .clock(clock),
    .cycle(cycle), .op(opcode), .imm(mmm), .bus_read(bus_control_1_bus_read),
    .bus_write(bus_control_1_bus_write), .bus_addr(bus_control_1_bus_addr));
  Multiplexer #(.width(8), .enable("false")) multiplexer_1 (
    .in0(register_2_q), .in1(bus_control_1_bus_addr), .out(multiplexer_1_out), .sel(cycle));
  Comparator comparator_1 (.a(multiplexer_1_out), .b({8{1'b1}}), .eq(comparator_1_eq));  // open: gt, lt
  Comparator #(.width(4)) comparator_2 (.a(opcode), .b(4'b1110), .eq(comparator_2_eq));  // open: gt, lt
  Comparator #(.width(4)) comparator_3 (.a(opcode), .b(4'b1100), .eq(comparator_3_eq));  // open: gt, lt
  Comparator comparator_4 (.a(mmm), .b({8{1'b1}}), .eq(comparator_4_eq));  // open: gt, lt
  Multiplexer #(.width(16), .enable("false")) multiplexer_2 (
    .in0(ram_1_data), .in1(bit_extender_2_out), .out(alu_1_bus_out), .sel(keydata));
  and and_3 (and_3_out, bus_control_1_bus_write, comparator_1_eq, comparator_2_eq);
  not not_2 (not_2_out, comparator_1_eq);
  not not_3 (not_3_out, cycle);
  not not_4 (not_4_out, clock);
  RAM #(.dataWidth(16), .bus("separate")) ram_1 (
    .addr(multiplexer_1_out), .din(data), .data(ram_1_data), .str(bus_control_1_bus_write),
    .clk(bus_control_1_bus_write), .ld(bus_control_1_bus_read), .clr(in_1));  // open: sel
  Bit_Extender #(.in_width(16), .out_width(7)) bit_extender_1 (.in(data), .out(bit_extender_1_out));
  TTY tty_1 (.data(bit_extender_1_out), .clk(and_3_out), .clr(Reset));  // open: we
  and and_4 (keydata, comparator_1_eq, comparator_3_eq, 1'b1);
  and and_5 (consume, not_2_out, comparator_3_eq, comparator_4_eq);
  nand nand_1 (enable, not_3_out, not_4_out);
  Keyboard keyboard_1 (.clk(consume), .re(enable), .clr(Reset), .data(keyboard_1_data));  // open: avail
  DotMatrix dotmatrix_1 (.col0(in_3), .col1(in_4), .col2(in_5), .col3(in_6), .col4(in_7));
  assign bit_extender_2_out = {{9{1'b0}}, keyboard_1_data};  // Bit_Extender bit_extender_2
  Register #(.width(16)) register_3 (.D(in_8), .clk(in_9));  // open: en, Q, clr

  // Notes on the sheet:
  //   Instruction
  //   Register
  //   Decoder
  //   Cycle
  //   Fetch/Decode/Execute cycle
  //   Regs
  //   ALU
  //   Bus
  //   Control
  //   Program
  //   Counter
  //   Bus
  //   RAM
  //   LED Matrix
endmodule

module _16_register_file (
  input  [15:0] d,
  input  Clk,
  input  [3:0] Rd,
  input  Clr,
  input  [3:0] Ra,
  input  [3:0] Rb,
  output [15:0] a,
  output [15:0] b
);

  wire demultiplexer_1_out0, demultiplexer_1_out1, demultiplexer_1_out2, demultiplexer_1_out3;
  wire [15:0] R0_R3_a, R0_R3_b, R4_R7_a, R4_R7_b, R8_Rb_a, R8_Rb_b, Rc_Rf_a, Rc_Rf_b;

  Demultiplexer #(.select(2), .enable("false")) demultiplexer_1 (
    .out0(demultiplexer_1_out0), .out1(demultiplexer_1_out1), .out2(demultiplexer_1_out2),
    .out3(demultiplexer_1_out3), .in(Clk), .sel(Rd[3:2]));
  three_register_file R0_R3 (
    .d(d), .Ck(demultiplexer_1_out0), .Rd(Rd[1:0]), .Clr(Clr), .Ra(Ra[1:0]), .Rb(Rb[1:0]), .a(R0_R3_a),
    .b(R0_R3_b));
  four_register_file R4_R7 (
    .d(d), .Ck(demultiplexer_1_out1), .Rd(Rd[1:0]), .Clr(Clr), .Ra(Ra[1:0]), .Rb(Rb[1:0]), .a(R4_R7_a),
    .b(R4_R7_b));
  four_register_file R8_Rb (
    .d(d), .Ck(demultiplexer_1_out2), .Rd(Rd[1:0]), .Clr(Clr), .Ra(Ra[1:0]), .Rb(Rb[1:0]), .a(R8_Rb_a),
    .b(R8_Rb_b));
  four_register_file Rc_Rf (
    .d(d), .Ck(demultiplexer_1_out3), .Rd(Rd[1:0]), .Clr(Clr), .Ra(Ra[1:0]), .Rb(Rb[1:0]), .a(Rc_Rf_a),
    .b(Rc_Rf_b));
  Multiplexer #(.select(2), .width(16), .enable("false")) multiplexer_1 (
    .in0(R0_R3_a), .in1(R4_R7_a), .in2(R8_Rb_a), .in3(Rc_Rf_a), .out(a), .sel(Ra[3:2]));
  Multiplexer #(.select(2), .width(16), .enable("false")) multiplexer_2 (
    .in0(R0_R3_b), .in1(R4_R7_b), .in2(R8_Rb_b), .in3(Rc_Rf_b), .out(b), .sel(Rb[3:2]));

  // Notes on the sheet:
  //   Data in
  //   Write data to register
  //   Note the splitter
  //   Which register?
  //   Reset everything
  //   Select the contents of two registers, Ra Rb
  //   Value of two registers selected
endmodule

module four_register_file (
  input  [15:0] d,
  input  Ck,
  input  [1:0] Rd,
  input  Clr,
  input  [1:0] Ra,
  input  [1:0] Rb,
  output [15:0] a,
  output [15:0] b
);

  wire demultiplexer_1_out0, demultiplexer_1_out1, demultiplexer_1_out2, demultiplexer_1_out3;
  wire [15:0] register_1_q, register_2_q, register_3_q, register_4_q;

  Demultiplexer #(.select(2), .enable("false")) demultiplexer_1 (
    .out0(demultiplexer_1_out0), .out1(demultiplexer_1_out1), .out2(demultiplexer_1_out2),
    .out3(demultiplexer_1_out3), .in(Ck), .sel(Rd));
  Register #(.width(16)) register_1 (.D(d), .Q(register_1_q), .clk(demultiplexer_1_out0), .clr(Clr));  // open: en
  Register #(.width(16)) register_2 (.D(d), .Q(register_2_q), .clk(demultiplexer_1_out1), .clr(Clr));  // open: en
  Register #(.width(16)) register_3 (.D(d), .Q(register_3_q), .clk(demultiplexer_1_out2), .clr(Clr));  // open: en
  Register #(.width(16)) register_4 (.D(d), .Q(register_4_q), .clk(demultiplexer_1_out3), .clr(Clr));  // open: en
  Multiplexer #(.select(2), .width(16), .enable("false")) multiplexer_1 (
    .in0(register_1_q), .in1(register_2_q), .in2(register_3_q), .in3(register_4_q), .out(a), .sel(Ra));
  Multiplexer #(.select(2), .width(16), .enable("false")) multiplexer_2 (
    .in0(register_1_q), .in1(register_2_q), .in2(register_3_q), .in3(register_4_q), .out(b), .sel(Rb));

  // Notes on the sheet:
  //   Data in
  //   Write signal
  //   Select register to write to
  //   Reset
  //   Values of selected registers
  //   Registers to select to read from
endmodule

module three_register_file (
  input  [15:0] d,
  input  Ck,
  input  [1:0] Rd,
  input  Clr,
  input  [1:0] Ra,
  input  [1:0] Rb,
  output [15:0] a,
  output [15:0] b
);

  wire demultiplexer_1_out1, demultiplexer_1_out2, demultiplexer_1_out3;
  wire [15:0] register_1_q, register_2_q, register_3_q;

  Demultiplexer #(.select(2), .enable("false")) demultiplexer_1 (
    .out1(demultiplexer_1_out1), .out2(demultiplexer_1_out2), .out3(demultiplexer_1_out3), .in(Ck), .sel(Rd));  // open: out0
  Register #(.width(16)) register_1 (.D(d), .Q(register_1_q), .clk(demultiplexer_1_out1), .clr(Clr));  // open: en
  Register #(.width(16)) register_2 (.D(d), .Q(register_2_q), .clk(demultiplexer_1_out2), .clr(Clr));  // open: en
  Register #(.width(16)) register_3 (.D(d), .Q(register_3_q), .clk(demultiplexer_1_out3), .clr(Clr));  // open: en
  Multiplexer #(.select(2), .width(16), .enable("false")) multiplexer_1 (
    .in0({16{1'b0}}), .in1(register_1_q), .in2(register_2_q), .in3(register_3_q), .out(a), .sel(Ra));
  Multiplexer #(.select(2), .width(16), .enable("false")) multiplexer_2 (
    .in0({16{1'b0}}), .in1(register_1_q), .in2(register_2_q), .in3(register_3_q), .out(b), .sel(Rb));

  // Notes on the sheet:
  //   R0
  //   R1
  //   R2
  //   R3
endmodule

module ALU (
  input  [15:0] a,
  input  [15:0] b,
  input  [3:0] op,
  input  [7:0] imm,
  input  enable,
  output [15:0] bus_out
);

  wire [15:0] adder_1_out, and_1_out, divider_1_out, multiplexer_1_out, multiplier_1_out, or_1_out,
       subtractor_1_out, xnor_1_out;

  Adder #(.width(16)) adder_1 (.a(a), .b(b), .out(adder_1_out));  // open: cin, cout
  Subtractor #(.width(16)) subtractor_1 (.a(a), .b(b), .out(subtractor_1_out));  // open: bin, bout
  Multiplier #(.width(16)) multiplier_1 (.a(a), .b(b), .out(multiplier_1_out));  // open: cin, cout
  Divider #(.width(16)) divider_1 (.a(a), .b(b), .out(divider_1_out));  // open: upper, rem
  assign and_1_out = a & b;  // AND_Gate and_1, 16 bits wide
  assign or_1_out = a | b;  // OR_Gate or_1, 16 bits wide
  assign xnor_1_out = ~(a ^ b);  // XNOR_Gate xnor_1, 16 bits wide
  Multiplexer #(.select(3), .width(16), .enable("false")) multiplexer_1 (
    .in0(adder_1_out), .in1(subtractor_1_out), .in2(multiplier_1_out), .in3(divider_1_out), .in4(and_1_out),
    .in5(or_1_out), .in6(xnor_1_out), .in7({{9{imm[7]}}, imm[6:0]}), .out(multiplexer_1_out), .sel(op[2:0]));
  assign bus_out = enable ? multiplexer_1_out : 16'bz;  // Controlled_Buffer controlled_buffer_1

  // Notes on the sheet:
  //   (sign extend)
endmodule

module PC_control (
  input  [3:0] op,
  input  [15:0] a,
  input  [7:0] imm,
  input  [7:0] PC_old,
  output [7:0] PC_new
);

  wire and_1_out, comparator_1_eq, comparator_1_gt, comparator_1_lt, multiplexer_1_out, not_1_out, not_2_out;
  wire [7:0] adder_1_out;

  Comparator #(.width(16)) comparator_1 (
    .a(a), .b({16{1'b0}}), .gt(comparator_1_gt), .eq(comparator_1_eq), .lt(comparator_1_lt));
  and and_1 (and_1_out, op[3], not_1_out, multiplexer_1_out);
  not not_1 (not_1_out, op[2]);
  Adder adder_1 (.a(8'h1), .b(PC_old), .out(adder_1_out));  // open: cin, cout
  not not_2 (not_2_out, comparator_1_eq);
  Multiplexer #(.select(2), .enable("false")) multiplexer_1 (
    .in0(comparator_1_eq), .in1(not_2_out), .in2(comparator_1_gt), .in3(comparator_1_lt),
    .out(multiplexer_1_out), .sel(op[1:0]));
  Multiplexer #(.width(8), .enable("false")) multiplexer_2 (
    .in0(adder_1_out), .in1(imm), .out(PC_new), .sel(and_1_out));

  // Notes on the sheet:
  //   Opcode
  //   Location to jump to
  //   Increment the old Program counter
  //   Register a
  //   Perform conditional goto
  //   The opcode determines which comparison to use
  //   New program counter
endmodule

module bus_control (
  input  [15:0] a,
  input  clock,
  input  cycle,
  input  [3:0] op,
  input  [7:0] imm,
  output reg_write,
  output ALU_enable,
  output bus_read,
  output bus_write,
  output [7:0] bus_addr
);

  wire and_1_out, and_2_out, and_3_out, not_1_out, not_2_out, not_3_out, or_1_out;

  not not_1 (not_1_out, op[1]);
  not not_2 (not_2_out, op[3]);
  and and_1 (and_1_out, op[3], op[2], not_1_out);
  and and_2 (and_2_out, op[3], op[2], op[1]);
  and and_3 (and_3_out, clock, cycle);
  or or_1 (or_1_out, not_2_out, and_1_out);
  not not_3 (not_3_out, cycle);
  and and_4 (reg_write, or_1_out, and_3_out);
  and and_5 (ALU_enable, not_2_out, cycle);
  or or_2 (bus_read, and_1_out, not_3_out);
  and and_6 (bus_write, and_2_out, and_3_out);
  Multiplexer #(.width(8), .enable("false")) multiplexer_1 (.in0(imm), .in1(a[7:0]), .out(bus_addr), .sel(op[0]));

  // Notes on the sheet:
  //   Implements Load/Store in the CPU
endmodule

module Decoder (
  input  [15:0] instruction,
  output [3:0] opcode,
  output [3:0] operand1,
  output [3:0] operand2,
  output [3:0] operand3,
  output [7:0] immediate
);

  Multiplexer #(.width(4), .enable("false")) multiplexer_1 (
    .in0(instruction[7:4]), .in1(instruction[11:8]), .out(operand2), .sel(instruction[15]));

  assign immediate = instruction[7:0];
  assign opcode = instruction[15:12];
  assign operand1 = instruction[11:8];
  assign operand3 = instruction[3:0];

  // Notes on the sheet:
  //   The MUX copies operand1 to operand2 for program and bus control
endmodule

module Data_Path (
  input  [15:0] \input ,
  input  write,
  input  read,
  input  [3:0] destination,
  input  reset,
  input  [3:0] Ra,
  input  [3:0] Rb,
  input  [3:0] opcode,
  input  [7:0] immediate,
  input  enable_alu,
  output [15:0] \output 
);

  wire [15:0] multiplexer_1_out, n16_register_file_1_a, n16_register_file_1_b;

  Multiplexer #(.width(16), .enable("false")) multiplexer_1 (
    .in0(\output ), .in1(\input ), .out(multiplexer_1_out), .sel(read));
  _16_register_file u_16_register_file_1 (
    .d(multiplexer_1_out), .Clk(write), .Rd(destination), .Clr(reset), .Ra(Ra), .Rb(Rb),
    .a(n16_register_file_1_a), .b(n16_register_file_1_b));
  ALU alu_1 (
    .a(n16_register_file_1_a), .b(n16_register_file_1_b), .op(opcode), .imm(immediate), .enable(enable_alu),
    .bus_out(\output ));
endmodule
