// Logisim project data-path.circ as structural Verilog: 4 circuits, main circuit main
module main (
);

  DataPath datapath_1 ();  // open: external_data, Ra, write_data, destination_register, data_source, Rb, clear, opcode, alu_out
endmodule

module ALU (
  input  [31:0] a,
  input  [31:0] b,
  input  [1:0] opcode,
  output [31:0] \output 
);

  wire [31:0] adder_1_out, and_1_out, multiplier_1_out, undriven;

  Adder #(.width(32)) adder_1 (.a(a), .b(b), .out(adder_1_out));  // open: cin, cout
  Multiplier #(.width(32)) multiplier_1 (.a(a), .b(b), .out(multiplier_1_out));  // open: cin, cout
  assign and_1_out = a & b;  // AND_Gate and_1, 32 bits wide
  Multiplexer #(.select(2), .width(32), .enable("false")) multiplexer_1 (
    .in0(adder_1_out), .in1(multiplier_1_out), .in2(and_1_out), .in3(undriven), .out(\output ), .sel(opcode));
endmodule

module Registers (
  input  [31:0] data_in,
  input  [1:0] Ra,
  input  write_data,
  input  [1:0] destination_register,
  input  [1:0] Rb,
  input  clear,
  output [31:0] a,
  output [31:0] b
);

  wire demultiplexer_1_out0, demultiplexer_1_out1, demultiplexer_1_out2, demultiplexer_1_out3;
  wire [31:0] register_1_q, register_2_q, register_3_q, register_4_q;

  Demultiplexer #(.select(2), .enable("false")) demultiplexer_1 (
    .out0(demultiplexer_1_out0), .out1(demultiplexer_1_out1), .out2(demultiplexer_1_out2),
    .out3(demultiplexer_1_out3), .in(write_data), .sel(destination_register));
  Register #(.width(32)) register_1 (
    .D(data_in), .Q(register_1_q), .clk(demultiplexer_1_out0), .clr(clear));  // open: en
  Register #(.width(32)) register_2 (
    .D(data_in), .Q(register_2_q), .clk(demultiplexer_1_out1), .clr(clear));  // open: en
  Register #(.width(32)) register_3 (
    .D(data_in), .Q(register_3_q), .clk(demultiplexer_1_out2), .clr(clear));  // open: en
  Register #(.width(32)) register_4 (
    .D(data_in), .Q(register_4_q), .clk(demultiplexer_1_out3), .clr(clear));  // open: en
  Multiplexer #(.select(2), .width(32), .enable("false")) multiplexer_1 (
    .in0(register_1_q), .in1(register_2_q), .in2(register_3_q), .in3(register_4_q), .out(a), .sel(Ra));
  Multiplexer #(.select(2), .width(32), .enable("false")) multiplexer_2 (
    .in0(register_1_q), .in1(register_2_q), .in2(register_3_q), .in3(register_4_q), .out(b), .sel(Rb));
endmodule

module DataPath (
  input  [31:0] external_data,
  input  [1:0] Ra,
  input  write_data,
  input  [1:0] destination_register,
  input  data_source,
  input  [1:0] Rb,
  input  clear,
  input  [1:0] opcode,
  output [31:0] alu_out
);

  wire [31:0] multiplexer_1_out, registers_1_a, registers_1_b;

  Multiplexer #(.width(32), .enable("false")) multiplexer_1 (
    .in0(alu_out), .in1(external_data), .out(multiplexer_1_out), .sel(data_source));
  Registers registers_1 (
    .data_in(multiplexer_1_out), .Ra(Ra), .write_data(write_data),
    .destination_register(destination_register), .Rb(Rb), .clear(clear), .a(registers_1_a), .b(registers_1_b));
  ALU alu_1 (.a(registers_1_a), .b(registers_1_b), .opcode(opcode), .\output (alu_out));
endmodule
