// Logisim project example.circ as structural Verilog: 3 circuits, main circuit main
module main (
  input  A,
  input  B,
  output out_3
);

  wire nor_1_out;

  and Here_s_the_AND_gate (out_3, A, B);
  nor nor_1 (nor_1_out, A, B);

  // Notes on the sheet:
  //   Inputs
  //   Output
endmodule

module adder (
  input  a,
  input  b,
  input  cin,
  output out_4,
  output out_5
);

  wire adder_1_cout, adder_1_out;

  full_adder full_adder_1 (.a(a), .b(b), .cin(cin), .cout(out_4), .sum(out_5));
  Adder #(.width(1)) adder_1 (.a(a), .b(b), .out(adder_1_out), .cin(cin), .cout(adder_1_cout));
endmodule

module full_adder (
  input  a,
  input  b,
  input  cin,
  output cout,
  output sum
);

  wire and_1_out, and_2_out, and_3_out, and_4_out, and_5_out, and_6_out, and_7_out, not_1_out, not_2_out,
       not_3_out, not_4_out, not_5_out, not_6_out;

  and and_1 (and_1_out, b, cin);
  and and_2 (and_2_out, a, cin);
  and and_3 (and_3_out, a, b);
  not not_1 (not_1_out, a);
  not not_2 (not_2_out, b);
  not not_3 (not_3_out, a);
  not not_4 (not_4_out, cin);
  not not_5 (not_5_out, b);
  not not_6 (not_6_out, cin);
  or or_1 (cout, and_1_out, and_2_out, and_3_out);
  and and_4 (and_4_out, not_1_out, not_2_out, cin);
  and and_5 (and_5_out, not_3_out, b, not_4_out);
  and and_6 (and_6_out, a, not_5_out, not_6_out);
  and and_7 (and_7_out, a, b, cin);
  or or_2 (sum, and_4_out, and_5_out, and_6_out, and_7_out);
endmodule
