// Logisim project lab1.circ as structural Verilog
module something1 (
  input  a2,
  input  a1,
  input  a0,
  output result
);

  wire nand_1_out, not_1_out, not_2_out;

  not not_1 (not_1_out, a2);
  not not_2 (not_2_out, a1);
  or or_1 (result, not_1_out, not_2_out);
  nand nand_1 (nand_1_out, a2, a1);

  // Notes on the sheet:
  //   a1'+a2' = (a1a2)'
endmodule

module something2 (
  input  [2:0] a
);

  wire multiplexer_1_out;

  Multiplexer #(.select(3), .enable("false")) multiplexer_1 (
    .in0(1'b1), .in1(1'b1), .in2(1'b1), .in3(1'b1), .in4(1'b1), .in5(1'b1), .in6(1'b0), .in7(1'b0),
    .out(multiplexer_1_out), .sel(a));
endmodule

module something3 (
  input  [2:0] a
);

  wire rom_1_data;

  ROM #(.addrWidth(3), .dataWidth(1)) rom_1 (.addr(a), .data(rom_1_data));  // open: sel

  // Notes on the sheet:
  //   contents of rom_1 (hex, n*v repeats v):
  //   6*1
endmodule
