// Logisim project plexer-logic.circ as structural Verilog: 3 circuits, main circuit main
module main (
  input  select,
  input  x,
  input  y,
  input  z,
  output random,
  output random_2,
  output random_3
);

  wire not_1_out, undriven, undriven_2;

  Multiplexer #(.enable("false")) multiplexer_1 (.in0(undriven), .in1(undriven_2), .out(random), .sel(select));
  not not_1 (not_1_out, z);
  Multiplexer #(.select(3), .enable("false")) multiplexer_2 (
    .in0(1'b1), .in1(1'b1), .in2(1'b0), .in3(1'b1), .in4(1'b1), .in5(1'b1), .in6(1'b1), .in7(1'b0),
    .out(random_3), .sel({x, y, z}));
  Multiplexer #(.select(2), .enable("false")) multiplexer_3 (
    .in0(1'b1), .in1(z), .in2(1'b1), .in3(not_1_out), .out(random_2), .sel({x, y}));
endmodule

module random (
  input  x,
  input  y,
  input  z,
  output random
);

  wire and_1_out, and_2_out, not_1_out, not_2_out, not_3_out;

  not not_1 (not_1_out, x);
  not not_2 (not_2_out, z);
  not not_3 (not_3_out, y);
  and and_1 (and_1_out, not_1_out, z);
  and and_2 (and_2_out, x, not_2_out);
  or or_1 (random, not_3_out, and_1_out, and_2_out);
endmodule

module rom (
  input  x,
  input  y,
  input  z,
  output out_4
);

  ROM #(.addrWidth(3), .dataWidth(1)) rom_1 (.addr({x, y, z}), .data(out_4));  // open: sel

  // Notes on the sheet:
  //   contents of rom_1 (hex, n*v repeats v):
  //   1 1 0 4*1
endmodule
