// Logisim project random-state-machine.circ as structural Verilog: 1 circuit, main circuit main
module main (
  input  in_1,
  input  in_2,
  output out_3
);

  wire clock_1_out;
  wire [2:1] register_1_q, rom_1_data;

  ROM #(.addrWidth(3), .dataWidth(3)) rom_1 (.addr({register_1_q, in_1}), .data({rom_1_data, out_3}));  // open: sel
  Clock clock_1 (.out(clock_1_out));
  Register #(.width(2)) register_1 (.D(rom_1_data), .Q(register_1_q), .clk(clock_1_out), .clr(in_2));  // open: en

  // Notes on the sheet:
  //   contents of rom_1 (hex, n*v repeats v):
  //   0 4 6 4 3 6 7 6
endmodule
