// Logisim project sequential-logic.circ as structural Verilog: 1 circuit, main circuit main
module main (
  input  s,
  input  r,
  input  in_3,
  input  [7:0] in_4,
  output q,
  output q_prime,
  output out_7
);

  wire clock_1_out;
  wire [7:0] register_1_q;

  Clock clock_1 (.out(clock_1_out));
  nand nand_1 (q, s, q_prime);
  nand nand_2 (q_prime, q, r);
  D_Flip_Flop d_ff_1 (.clk(clock_1_out), .D(in_3), .Q(out_7));  // open: Qn, preset, en, reset
  Register register_1 (.D(in_4), .Q(register_1_q), .clk(clock_1_out));  // open: en, clr
  Hex_Digit_Display hex_digit_display_1 (.value(register_1_q[7:4]));  // open: dp
  Hex_Digit_Display hex_digit_display_2 (.value(register_1_q[3:0]));  // open: dp
endmodule
