// Logisim project traffic-light.circ as structural Verilog: 1 circuit, main circuit main
module main (
);

  wire clock_1_out, decoder_1_out0, decoder_1_out1, decoder_1_out2, decoder_2_out0, decoder_2_out1,
       decoder_2_out2;
  wire [2:0] register_1_q;
  wire [6:0] rom_1_data;

  ROM #(.addrWidth(3), .dataWidth(7)) rom_1 (.addr(register_1_q), .data(rom_1_data));  // open: sel
  Clock clock_1 (.out(clock_1_out));
  Register #(.width(3)) register_1 (.D(rom_1_data[6:4]), .Q(register_1_q), .clk(clock_1_out));  // open: en, clr
  Decoder #(.select(2), .enable("false")) decoder_1 (
    .out0(decoder_1_out0), .out1(decoder_1_out1), .out2(decoder_1_out2), .sel(rom_1_data[1:0]));  // open: out3
  Decoder #(.select(2), .enable("false")) decoder_2 (
    .out0(decoder_2_out0), .out1(decoder_2_out1), .out2(decoder_2_out2), .sel(rom_1_data[3:2]));  // open: out3
  LED led_1 (.in(decoder_1_out0));
  LED led_2 (.in(decoder_1_out1));
  LED led_3 (.in(decoder_1_out2));
  LED led_4 (.in(decoder_2_out0));
  LED led_5 (.in(decoder_2_out1));
  LED led_6 (.in(decoder_2_out2));

  // Notes on the sheet:
  //   contents of rom_1 (hex, n*v repeats v):
  //   18 28 34 42 52 62 71 8
endmodule
