// Logisim project Lab3.circ as structural Verilog: 1 circuit, main circuit main
module main (
  input  in_1,
  output [2:0] out_2,
  output out_3
);

  wire clock_1_out, dime_out, nickel_out, not_1_out, or_1_out, quarter_out;
  wire [1:0] priority_encoder_1_out;
  wire [2:0] state_q;
  wire [6:4] rom_1_data;

  Button nickel (.out(nickel_out));
  Priority_Encoder #(.select(2)) priority_encoder_1 (
    .in0(1'b0), .in1(nickel_out), .in2(dime_out), .in3(quarter_out), .out(priority_encoder_1_out));  // open: gs, en_out, en_in
  Button dime (.out(dime_out));
  Button quarter (.out(quarter_out));
  // Probe on priority_encoder_1_out
  Pull_Resistor pull_resistor_1 (.node(priority_encoder_1_out));
  ROM #(.addrWidth(5), .dataWidth(7)) rom_1 (
    .addr({state_q, priority_encoder_1_out}), .data({rom_1_data, out_3, out_2}));  // open: sel
  Clock clock_1 (.out(clock_1_out));
  or or_1 (or_1_out, in_1, clock_1_out);
  not not_1 (not_1_out, or_1_out);
  Register #(.width(3)) state (.D(rom_1_data), .Q(state_q), .clk(not_1_out));  // open: en, clr

  // Notes on the sheet:
  //   contents of rom_1 (hex, n*v repeats v):
  //   0 10 20 1 10 20 30 3 20 30 40 5 30 40 1 7 40 1 3 9
endmodule
