// Logisim project lab2.circ as structural Verilog: 1 circuit, main circuit main
module main (
  input  [1:0] in_1,
  input  in_2,
  input  in_3,
  output out_4,
  output [2:0] out_5
);

  wire clock_1_out, not_1_out, or_1_out;
  wire [4:2] register_1_q;
  wire [6:4] rom_1_data;

  ROM #(.addrWidth(5), .dataWidth(7)) rom_1 (
    .addr({register_1_q, in_1}), .data({rom_1_data, out_5, out_4}));  // open: sel
  not not_1 (not_1_out, or_1_out);
  or or_1 (or_1_out, clock_1_out, in_3);
  Clock clock_1 (.out(clock_1_out));
  Register #(.width(3)) register_1 (.D(rom_1_data), .Q(register_1_q), .clk(not_1_out), .clr(in_2));  // open: en

  // Notes on the sheet:
  //   contents of rom_1 (hex, n*v repeats v):
  //   0 10 20 1 10 20 30 3 20 30 40 5 30 40 5 30 40 1 7 40 1 3 9
endmodule
